# Fritzing sketch 24LC64 (saved by Fritzing 0.9.3b)
breadboards: 1

parts:
  IC1 = 24LC64 [package=THT]
  Componente1 = Arduino Nano (Rev3.0)

nets:
  N1: IC1.A0, IC1.A1, IC1.A2, IC1.0V, IC1.WP_-_Write_Protect, Componente1.GND
  N2: IC1.SDA_-_I2C_Data, Componente1.A4
  N3: IC1.SCL_-_I2C_Clock, Componente1.A5
  N4: IC1.+V, Componente1.5V
